# Fritzing sketch FritzingProtoboard (saved by Fritzing 0.9.2b)
breadboards: 2

parts:
  U2 = NodeMCU V1.0
  LED3 = RGB LED - (4 legs) [package="5 mm [THT]"]
  LED4 = RGB LED - (4 legs) [package="5 mm [THT]"]  # not connected
  T2 = LM35 Temperature Sensor [package="TO92 [THT]"]
  VCC2 = 4 x AAA Battery Mount

nets:
  N1: U2.D1, LED3.red_cathode
  N2: U2.D3, LED3.green_cathode
  N3: U2.D4, LED3.blue_cathode
  N4: U2.3V3, T2.+Vs
  GND: U2.GND, LED3.common_anode, T2.GND, VCC2.-
  N5: U2.Vin, VCC2.+
  N6: U2.A0, T2.Vout

notes:
  Avagroup - Thiiink IoT

custom parts:
  NodeMCU V1.0: ESP8266 based NodeMCU
