# Fritzing sketch FritzingProtoboard (saved by Fritzing 0.9.2b)
breadboards: 2

parts:
  LED1 = RGB LED - (4 legs) [package="5 mm [THT]"]
  T1 = LM35 Temperature Sensor [package="TO92 [THT]"]
  U1 = NodeMCU V1.0

nets:
  N1: LED1.red_cathode, U1.D1
  GND: LED1.common_anode, T1.GND, U1.GND
  N2: LED1.green_cathode, U1.D3
  N3: LED1.blue_cathode, U1.D4
  N4: T1.+Vs, U1.3V3
  N5: T1.Vout, U1.A0

notes:
  Avagroup - Thiiink IoT

custom parts:
  NodeMCU V1.0: ESP8266 based NodeMCU
